# Fritzing sketch quizboard_2_0 (saved by Fritzing 0.9.3b)
circuit board: 1.39778cm x 2.3706cm
circuit board: 8.46667cm x 5.64444cm
circuit board: 1.39778cm x 2.3706cm
breadboards: 5

parts:
  Bauteil1 = Arduino Uno (Rev3)
  LED1 = LED - 5mm [color="Green (565nm)" package="5 mm [THT]"]
  Kont_B = rounded female pin header, 4 pins [form="♀ (female rounded)"]
  Kont_C = rounded female pin header, 4 pins [form="♀ (female rounded)"]
  R37 = Resistor [tolerance=±5% resistance=10M package=THT]
  Kont_A = rounded female pin header, 4 pins [form="♀ (female rounded)"]
  R38 = Resistor [tolerance=±5% resistance=10M package=THT]
  R39 = Resistor [tolerance=±5% resistance=10M package=THT]
  R40 = Resistor [tolerance=±5% resistance=10M package=THT]
  R18 = Resistor [tolerance=±5% resistance=1M package=THT]
  R17 = Resistor [tolerance=±5% resistance=1M package=THT]
  R31 = Resistor [tolerance=±5% resistance=1M package=THT]
  R30 = Resistor [tolerance=±5% resistance=1M package=THT]
  R33 = Resistor [tolerance=±5% resistance=1M package=THT]
  LED_Shift = 74HC595 [package="DIP16 [THT]"]
  LED_Bus_Plug = male pin header, 5 pins [form="♂ (male)"]
  LED2 = LED - 5mm [color="Green (565nm)" package="5 mm [THT]"]
  LED3 = LED - 5mm [color="Green (565nm)" package="5 mm [THT]"]
  LED4 = LED - 5mm [color="Green (565nm)" package="5 mm [THT]"]
  LED5 = LED - 5mm [color="Green (565nm)" package="5 mm [THT]"]
  LED6 = LED - 5mm [color="Green (565nm)" package="5 mm [THT]"]
  LED7 = LED - 5mm [color="Green (565nm)" package="5 mm [THT]"]
  LED8 = LED - 5mm [color="Green (565nm)" package="5 mm [THT]"]
  7_Segment2 = 7 Segment Display
  7Seg_Shift = 74HC595 [package="DIP16 [THT]"]
  R41 = Resistor [tolerance=±5% resistance=220 package=THT]
  R42 = Resistor [tolerance=±5% resistance=220 package=THT]
  R43 = Resistor [tolerance=±5% resistance=220 package=THT]
  R44 = Resistor [tolerance=±5% resistance=220 package=THT]
  R45 = Resistor [tolerance=±5% resistance=220 package=THT]
  R46 = Resistor [tolerance=±5% resistance=220 package=THT]
  R47 = Resistor [tolerance=±5% resistance=220 package=THT]
  R48 = Resistor [tolerance=±5% resistance=220 package=THT]
  J2 = male pin header, 2 pins [form="♂ (male)"]
  J3 = male pin header, 2 pins [form="♂ (male)"]
  J4 = male pin header, 2 pins [form="♂ (male)"]
  J5 = male pin header, 2 pins [form="♂ (male)"]
  J6 = male pin header, 2 pins [form="♂ (male)"]
  J7 = male pin header, 2 pins [form="♂ (male)"]
  J1 = male pin header, 2 pins [form="♂ (male)"]
  J8 = male pin header, 3 pins [form="♂ (male)"]
  Select_Button_(Encoder_Push) = Pushbutton [package="[THT]"]
  Result_Button = Pushbutton [package="[THT]"]
  Plug_Shift = 74HC595 [package="DIP16 [THT]"]
  LED&Plug_Connector = female pin header, 17 pins [form="♀ (female)"]
  R49 = Resistor [tolerance=±5% resistance=220 package=THT]
  R50 = Resistor [tolerance=±5% resistance=220 package=THT]
  R51 = Resistor [tolerance=±5% resistance=220 package=THT]
  R52 = Resistor [tolerance=±5% resistance=220 package=THT]
  R53 = Resistor [tolerance=±5% resistance=220 package=THT]
  R54 = Resistor [tolerance=±5% resistance=220 package=THT]
  R55 = Resistor [tolerance=±5% resistance=220 package=THT]
  R56 = Resistor [tolerance=±5% resistance=220 package=THT]
  D1 = Rectifier Diode [part_number=1N4007 package="300 mil [THT]"]
  D2 = Rectifier Diode [part_number=1N4007 package="300 mil [THT]"]
  D3 = Rectifier Diode [part_number=1N4007 package="300 mil [THT]"]
  D4 = Rectifier Diode [part_number=1N4007 package="300 mil [THT]"]
  D5 = Rectifier Diode [part_number=1N4007 package="300 mil [THT]"]
  D6 = Rectifier Diode [part_number=1N4007 package="300 mil [THT]"]
  D7 = Rectifier Diode [part_number=1N4007 package="300 mil [THT]"]
  D8 = Rectifier Diode [part_number=1N4007 package="300 mil [THT]"]
  J18 = rounded female pin header, 1 pin [form="♀ (female rounded)"]
  R25 = Resistor [tolerance=±5% resistance=2M package=THT]
  J19 = rounded female pin header, 1 pin [form="♀ (female rounded)"]
  R34 = Resistor [tolerance=±5% resistance=2M package=THT]
  R35 = Resistor [tolerance=±5% resistance=2M package=THT]
  J20 = rounded female pin header, 1 pin [form="♀ (female rounded)"]
  R57 = Resistor [tolerance=±5% resistance=1M package=THT]
  R58 = Resistor [tolerance=±5% resistance=1M package=THT]
  J21 = rounded female pin header, 1 pin [form="♀ (female rounded)"]
  R36 = Resistor [tolerance=±5% resistance=2M package=THT]
  LED_Bus_Plug1 = male pin header, 5 pins [form="♂ (male)"]
  R32 = Resistor [tolerance=±5% resistance=1M package=THT]
  Kont_D = rounded female pin header, 4 pins [form="♀ (female rounded)"]
  Program_Select_Encoder = Rotary Encoder [package=THT]

nets:
  N1: Bauteil1.A0, R37.Pin_1, Kont_A.pin1, R17.Pin_0, R33.Pin_1, J18.pin1, R25.Pin_1
  N2: Bauteil1.A1, Kont_B.pin1, R38.Pin_1, R18.Pin_0, R30.Pin_1, J19.pin1, R34.Pin_1
  N3: Bauteil1.A2, Kont_C.pin1, R39.Pin_1, R31.Pin_1, R35.Pin_1, J20.pin1, R57.Pin_0
  N4: Bauteil1.A3, R40.Pin_1, R58.Pin_0, J21.pin1, R36.Pin_1, R32.Pin_1, Kont_D.pin1
  N5: Bauteil1.D8, Plug_Shift.ST_CP
  N6: Bauteil1.D9_PWM, Plug_Shift.SH_CP
  N7: Bauteil1.D10_PWM/SS, 7Seg_Shift.DS
  N8: Bauteil1.D11_PWM/MOSI, LED_Shift.ST_CP, LED_Bus_Plug.pin4, 7Seg_Shift.ST_CP, LED_Bus_Plug1.pin3
  N9: Bauteil1.D12/MISO, LED_Shift.SH_CP, LED_Bus_Plug.pin3, 7Seg_Shift.SH_CP, LED_Bus_Plug1.pin2
  GND: Bauteil1.GND, LED1.anode, R18.Pin_1, R17.Pin_1, LED_Shift.GND, LED_Shift.OE, LED_Bus_Plug.pin5, LED2.anode, LED3.anode, LED4.anode, LED5.anode, LED6.anode, LED7.anode, LED8.anode, 7Seg_Shift.GND, 7Seg_Shift.OE, J8.pin3, Select_Button_(Encoder_Push).Pin_1, Select_Button_(Encoder_Push).Pin_2, Result_Button.Pin_1, Result_Button.Pin_2, Plug_Shift.GND, Plug_Shift.OE, LED&Plug_Connector.pin17, R57.Pin_1, R58.Pin_1, LED_Bus_Plug1.pin4, Program_Select_Encoder.EncoderPinC
  N10: Bauteil1.D2, Result_Button.Pin_4
  N11: Bauteil1.D3_PWM, Select_Button_(Encoder_Push).Pin_3, Select_Button_(Encoder_Push).Pin_4
  N12: Bauteil1.D5_PWM, Program_Select_Encoder.EncoderPinB
  N13: Bauteil1.D6_PWM, Program_Select_Encoder.EncoderPinA
  N14: Bauteil1.D7, Plug_Shift.DS
  VCC: Bauteil1.5V, LED_Shift.MR, LED_Shift.VCC, LED_Bus_Plug.pin2, 7_Segment2.common_anode, 7Seg_Shift.MR, 7Seg_Shift.VCC, Plug_Shift.MR, Plug_Shift.VCC, LED_Bus_Plug1.pin1
  N15: LED1.cathode, J8.pin1, LED&Plug_Connector.pin16, R49.Pin_0
  N16: Kont_B.pin2, R30.Pin_0
  N17: Kont_B.pin3, R34.Pin_0
  N18: Kont_B.pin4, R38.Pin_0
  N19: Kont_C.pin2, R31.Pin_0
  N20: Kont_C.pin3, R35.Pin_0
  N21: Kont_C.pin4, R39.Pin_0
  N22: R37.Pin_0, Kont_A.pin4
  N23: Kont_A.pin2, R33.Pin_0
  N24: Kont_A.pin3, R25.Pin_0
  N25: R40.Pin_0, Kont_D.pin4
  N26: LED_Shift.Q1, R50.Pin_1
  N27: LED_Shift.Q2, R51.Pin_1
  N28: LED_Shift.Q3, R52.Pin_1
  N29: LED_Shift.Q4, R53.Pin_1
  N30: LED_Shift.Q5, R54.Pin_1
  N31: LED_Shift.Q6, R55.Pin_1
  N32: LED_Shift.Q7, R56.Pin_1
  N33: LED_Shift.DS, LED_Bus_Plug.pin1, 7Seg_Shift.Q7', LED_Bus_Plug1.pin5
  N34: LED_Shift.Q0, R49.Pin_1
  N35: LED2.cathode, J7.pin1, LED&Plug_Connector.pin14, R50.Pin_0
  N36: LED3.cathode, J6.pin1, LED&Plug_Connector.pin12, R51.Pin_0
  N37: LED4.cathode, J5.pin1, LED&Plug_Connector.pin10, R52.Pin_0
  N38: LED5.cathode, J4.pin1, LED&Plug_Connector.pin8, R53.Pin_0
  N39: LED6.cathode, J3.pin1, LED&Plug_Connector.pin6, R54.Pin_0
  N40: LED7.cathode, J2.pin1, LED&Plug_Connector.pin4, R55.Pin_0
  N41: LED8.cathode, J1.pin1, LED&Plug_Connector.pin2, R56.Pin_0
  N42: 7_Segment2.Segment_E, R47.Pin_1
  N43: 7_Segment2.Segment_D, R48.Pin_1
  N44: 7_Segment2.Segment_C, R45.Pin_1
  N45: 7_Segment2.Segment_DP, R46.Pin_1
  N46: 7_Segment2.Segment_B, R44.Pin_1
  N47: 7_Segment2.Segment_A, R43.Pin_1
  N48: 7_Segment2.Segment_F, R42.Pin_0
  N49: 7_Segment2.Segment_G, R41.Pin_1
  N50: 7Seg_Shift.Q1, R44.Pin_0
  N51: 7Seg_Shift.Q2, R43.Pin_0
  N52: 7Seg_Shift.Q3, R41.Pin_0
  N53: 7Seg_Shift.Q4, R47.Pin_0
  N54: 7Seg_Shift.Q5, R46.Pin_0
  N55: 7Seg_Shift.Q6, R45.Pin_0
  N56: 7Seg_Shift.Q7, R48.Pin_0
  N57: 7Seg_Shift.Q0, R42.Pin_1
  N58: J2.pin2, LED&Plug_Connector.pin3, D7.cathode
  N59: J3.pin2, LED&Plug_Connector.pin5, D6.cathode
  N60: J4.pin2, LED&Plug_Connector.pin7, D5.cathode
  N61: J5.pin2, LED&Plug_Connector.pin9, D4.cathode
  N62: J6.pin2, LED&Plug_Connector.pin11, D3.cathode
  N63: J7.pin2, LED&Plug_Connector.pin13, D2.cathode
  N64: J1.pin2, LED&Plug_Connector.pin1, D8.cathode
  N65: J8.pin2, LED&Plug_Connector.pin15, D1.cathode
  N66: Plug_Shift.Q1, D2.anode
  N67: Plug_Shift.Q2, D3.anode
  N68: Plug_Shift.Q3, D4.anode
  N69: Plug_Shift.Q4, D5.anode
  N70: Plug_Shift.Q5, D6.anode
  N71: Plug_Shift.Q6, D7.anode
  N72: Plug_Shift.Q7, D8.anode
  N73: Plug_Shift.Q0, D1.anode
  N74: R36.Pin_0, Kont_D.pin3
  N75: R32.Pin_0, Kont_D.pin2
